# Fritzing sketch ePaperStation (saved by Fritzing 0.9.3b)
breadboards: 1

parts:
  Bauteil1 = ESP-WROOM-32 [ESP-32S] Module [part_number=ESP-WROOM-32]
  Bauteil2 = Adafruit ADS1115 16Bit I2C ADC [part_number="Adafruit #1085"]
  U1 = LIPO-1000mAh [package=lipo-1000]
  D1 = Diode [package=diode-hv]
  D2 = Diode [package=diode-hv]

nets:
  GND: Bauteil1.GND, Bauteil2.ADDR, Bauteil2.GND, U1.-
  N1: Bauteil1.3V3, D1.A
  N2: Bauteil1.SD0, Bauteil2.SDA
  N3: Bauteil1.SD1, Bauteil2.SCL
  N4: Bauteil2.AIN0, U1.+, D2.A
  N5: Bauteil2.VDD, D1.C, D2.C

custom parts:
  ESP-WROOM-32 [ESP-32S] Module: Espressif ESP-WROOM-32 WiFi/Bluetooth LE microcontroller module also known as the Ai-Thinker ESP-32S module with similar formfactor. The ESP32 is a microcontroller chip with WiFi and BLE capabilities. The chip is developed by Espressif and is the successor to the popular ESP8266 WiFi module.
  Adafruit ADS1115 16Bit I2C ADC: For microcontrollers without an analog-to-digital converter or when you want a higher-precision ADC, the ADS1115 provides 16-bit precision at 860 samples/second over I2C. The chip can be configured as 4 single-ended input channels, or two differential channels. As a nice bonus, it even includes a programmable gain amplifier, up to x16, to help boost up smaller single/differential signals to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
